// Logisim project Lab3a1037.circ as structural Verilog: 11 circuits, main circuit main
module main (
);

  wire CLK, clock_1_out, cpu_1_halt, decimaldisplaycontrol_1_sign, frontpanelcontroller_1_runhalt, Reset,
       RunStop_out, Step_out;
  wire [3:0] cpu_1_aluflags, cpu_1_flags, decimaldisplaycontrol_1_d0, decimaldisplaycontrol_1_d1,
       decimaldisplaycontrol_1_d2, decimaldisplaycontrol_1_d3, decimaldisplaycontrol_1_d4, decimalio_1_data,
       decimalio_1_data_2, decimalio_1_data_3, decimalio_1_data_4;
  wire [15:0] cpu_1_alua, cpu_1_alub, cpu_1_aluresult, cpu_1_imaddress, cpu_1_imdata, cpu_1_writeback,
       DMAddress, DMData, IM_data;

  Clock clock_1 (.out(clock_1_out));
  ROM #(.addrWidth(16), .dataWidth(16)) IM (.addr(cpu_1_imaddress), .data(IM_data));
  FrontPanelController frontpanelcontroller_1 (
    .Clk(clock_1_out), .Run(RunStop_out), .Step(Step_out), .Reset(Reset), .Halt(cpu_1_halt), .CpuClk(CLK),
    .RunHalt(frontpanelcontroller_1_runhalt));
  CPU cpu_1 (
    .CLK(CLK), .Reset(Reset), .IMDataIn(IM_data), .Halt(cpu_1_halt), .IMAddress(cpu_1_imaddress),
    .IMData(cpu_1_imdata), .DMAddress(DMAddress), .DMData(DMData), .WriteBack(cpu_1_writeback),
    .Flags(cpu_1_flags), .AluA(cpu_1_alua), .AluB(cpu_1_alub), .ALUResult(cpu_1_aluresult),
    .ALUFlags(cpu_1_aluflags));
  LED led_1 (.in(cpu_1_flags[3]));
  LED led_2 (.in(cpu_1_flags[2]));
  LED led_3 (.in(cpu_1_flags[1]));
  LED led_4 (.in(cpu_1_flags[0]));
  Hex_Digit_Display hex_digit_display_1 (.value(cpu_1_alua[15:12]));  // open: dp
  LED led_5 (.in(cpu_1_halt));
  Hex_Digit_Display hex_digit_display_2 (.value(cpu_1_imaddress[15:12]));  // open: dp
  Hex_Digit_Display hex_digit_display_3 (.value(cpu_1_imaddress[11:8]));  // open: dp
  Hex_Digit_Display hex_digit_display_4 (.value(cpu_1_imdata[15:12]));  // open: dp
  Hex_Digit_Display hex_digit_display_5 (.value(cpu_1_imdata[11:8]));  // open: dp
  Hex_Digit_Display hex_digit_display_6 (.value(cpu_1_alua[11:8]));  // open: dp
  Hex_Digit_Display hex_digit_display_7 (.value(cpu_1_alua[7:4]));  // open: dp
  LED N (.in(cpu_1_aluflags[3]));
  LED Z (.in(cpu_1_aluflags[2]));
  LED C (.in(cpu_1_aluflags[1]));
  LED led_6 (.in(frontpanelcontroller_1_runhalt));
  Button RunStop (.out(RunStop_out));
  Hex_Digit_Display hex_digit_display_8 (.value(cpu_1_imaddress[7:4]));  // open: dp
  Hex_Digit_Display hex_digit_display_9 (.value(cpu_1_imaddress[3:0]));  // open: dp
  Hex_Digit_Display hex_digit_display_10 (.value(cpu_1_imdata[7:4]));  // open: dp
  // Hex_Digit_Display hex_digit_display_11: pin names not known; wires that end beside it: cpu_1_imdata[3:0]
  Hex_Digit_Display hex_digit_display_12 (.value(cpu_1_alua[3:0]));  // open: dp
  LED V (.in(cpu_1_aluflags[0]));
  Button Step (.out(Step_out));
  Hex_Digit_Display hex_digit_display_13 (.value(DMAddress[15:12]));  // open: dp
  Hex_Digit_Display hex_digit_display_14 (.value(DMData[15:12]));  // open: dp
  Hex_Digit_Display hex_digit_display_15 (.value(cpu_1_writeback[15:12]));  // open: dp
  Hex_Digit_Display hex_digit_display_16 (.value(cpu_1_alub[15:12]));  // open: dp
  Hex_Digit_Display hex_digit_display_17 (.value(cpu_1_aluresult[15:12]));  // open: dp
  Button u_Reset (.out(Reset));
  Hex_Digit_Display hex_digit_display_18 (.value(DMAddress[11:8]));  // open: dp
  Hex_Digit_Display hex_digit_display_19 (.value(DMAddress[7:4]));  // open: dp
  Hex_Digit_Display hex_digit_display_20 (.value(DMData[11:8]));  // open: dp
  Hex_Digit_Display hex_digit_display_21 (.value(DMData[7:4]));  // open: dp
  Hex_Digit_Display hex_digit_display_22 (.value(cpu_1_writeback[11:8]));  // open: dp
  Hex_Digit_Display hex_digit_display_23 (.value(cpu_1_writeback[7:4]));  // open: dp
  Hex_Digit_Display hex_digit_display_24 (.value(cpu_1_alub[11:8]));  // open: dp
  Hex_Digit_Display hex_digit_display_25 (.value(cpu_1_alub[7:4]));  // open: dp
  Hex_Digit_Display hex_digit_display_26 (.value(cpu_1_aluresult[11:8]));  // open: dp
  Hex_Digit_Display hex_digit_display_27 (.value(cpu_1_aluresult[7:4]));  // open: dp
  Hex_Digit_Display hex_digit_display_28 (.value(DMAddress[3:0]));  // open: dp
  Hex_Digit_Display hex_digit_display_29 (.value(DMData[3:0]));  // open: dp
  Hex_Digit_Display hex_digit_display_30 (.value(cpu_1_writeback[3:0]));  // open: dp
  Hex_Digit_Display hex_digit_display_31 (.value(cpu_1_alub[3:0]));  // open: dp
  Hex_Digit_Display hex_digit_display_32 (.value(cpu_1_aluresult[3:0]));  // open: dp
  _7_Segment_Display u_7_segment_display_1 (.g(decimaldisplaycontrol_1_sign));  // open: f, a, b, e, d, c, dp
  Hex_Digit_Display hex_digit_display_33 (.value(decimalio_1_data_4));  // open: dp
  Hex_Digit_Display hex_digit_display_34 (.value(decimaldisplaycontrol_1_d4));  // open: dp
  Hex_Digit_Display hex_digit_display_35 (.value(decimaldisplaycontrol_1_d3));  // open: dp
  Hex_Digit_Display hex_digit_display_36 (.value(decimalio_1_data_3));  // open: dp
  Hex_Digit_Display hex_digit_display_37 (.value(decimalio_1_data_2));  // open: dp
  Hex_Digit_Display hex_digit_display_38 (.value(decimaldisplaycontrol_1_d2));  // open: dp
  Hex_Digit_Display hex_digit_display_39 (.value(decimaldisplaycontrol_1_d1));  // open: dp
  Hex_Digit_Display hex_digit_display_40 (.value(decimalio_1_data));  // open: dp
  Hex_Digit_Display hex_digit_display_41 (.value(decimaldisplaycontrol_1_d0));  // open: dp
  DecimalDisplayControl decimaldisplaycontrol_1 (
    .DataIn({decimalio_1_data_4, decimalio_1_data_3, decimalio_1_data_2, decimalio_1_data}),
    .D0(decimaldisplaycontrol_1_d0), .D1(decimaldisplaycontrol_1_d1), .D2(decimaldisplaycontrol_1_d2),
    .D3(decimaldisplaycontrol_1_d3), .D4(decimaldisplaycontrol_1_d4), .Sign(decimaldisplaycontrol_1_sign));
  DecimalIO decimalio_1 (
    .DMData(DMData), .DMAddress(DMAddress), .CLK(CLK), .Reset(Reset),
    .Data({decimalio_1_data_4, decimalio_1_data_3, decimalio_1_data_2, decimalio_1_data}));

  // Notes on the sheet:
  //   contents of IM (hex, n*v repeats v):
  //   9004 a002 205a 22a1 246a 2672 2889 2a99 2c62 2e6a 3072 32c8 345a 3662 386a 3a72 3c4a 3e42
  //   N  Z  C  V
  //   Latched Flags
  //   HALT
  //   Instruction Memory
  //   alARM
  //   ALU A Input
  //   ALU Flags
  //   Data Memory
  //   WriteBack
  //   ALU B Input
  //   ALU Result
endmodule

module CPU (
  input  CLK,
  input  Reset,
  input  [15:0] IMDataIn,
  output Halt,
  output [15:0] IMAddress,
  output [15:0] IMData,
  output [15:0] DMAddress,
  output [15:0] DMData,
  output [15:0] WriteBack,
  output [3:0] Flags,
  output [15:0] AluA,
  output [15:0] AluB,
  output [15:0] ALUResult,
  output [3:0] ALUFlags
);

  wire Cin, CLKin, d_ff_1_qn, JMP, Mem2Reg, MemW, MoveFlag, Offset, RegW, STOP, WBranchOrResult, WriteFlag,
       WriteResult;
  wire [2:0] multiplexer_3_out, multiplexer_6_out;
  wire [3:0] ALUOp, multiplexer_2_out;
  wire [15:0] bit_extender_1_out, bit_extender_2_out, datamemory_1_dmdataout, instructionfetchunit_1_pcplus1,
       multiplexer_1_out, multiplexer_4_out, multiplexer_5_out, multiplexer_7_out, multiplexer_9_out,
       multiplexer_10_out, registerfile_1_rd2;

  Multiplexer #(.width(16)) multiplexer_1 (.in0(ALUResult), .in1(AluB), .out(multiplexer_1_out), .sel(WBranchOrResult));
  D_Flip_Flop #(.trigger("falling")) d_ff_1 (
    .D(STOP), .clk(CLKin), .Q(Halt), .Qn(d_ff_1_qn), .reset(Reset));  // open: preset
  and and_1 (CLKin, d_ff_1_qn, CLK);
  Multiplexer #(.width(4)) multiplexer_2 (.in0(ALUFlags), .in1(AluA[3:0]), .out(multiplexer_2_out), .sel(MoveFlag));
  InstructionFetchUnit instructionfetchunit_1 (
    .WBBus(multiplexer_1_out), .JMP(JMP), .CLK(CLKin), .RESET(Reset), .IMAddress(IMAddress),
    .PCPlus1(instructionfetchunit_1_pcplus1));
  Multiplexer #(.width(3)) multiplexer_3 (
    .in0(IMDataIn[5:3]), .in1(IMDataIn[14:12]), .out(multiplexer_3_out), .sel(IMDataIn[15]));
  Multiplexer #(.width(16)) multiplexer_4 (.in0(AluA), .in1(ALUResult), .out(multiplexer_4_out), .sel(WriteResult));
  Multiplexer #(.width(16)) multiplexer_5 (
    .in0(multiplexer_4_out), .in1(AluB), .out(multiplexer_5_out), .sel(IMDataIn[15]));
  assign bit_extender_1_out = {{12{1'b0}}, Flags};  // Bit_Extender bit_extender_1
  Multiplexer #(.width(3)) multiplexer_6 (.in0(IMDataIn[8:6]), .in1(3'b111), .out(multiplexer_6_out), .sel(JMP));
  DecoderController decodercontroller_1 (
    .CBits(IMDataIn[15:9]), .Flags(multiplexer_2_out), .CLK(CLKin), .R(Reset), .MoveFlag(MoveFlag),
    .ALUOp(ALUOp), .WriteResult(WriteResult), .RegW(RegW), .Cin(Cin), .LatchFlags(Flags), .JMP(JMP),
    .STOP(STOP), .WBranchOrResult(WBranchOrResult), .WriteFlag(WriteFlag), .MemW(MemW), .Offset(Offset),
    .Mem2Reg(Mem2Reg));
  Multiplexer #(.width(16)) multiplexer_7 (
    .in0(multiplexer_5_out), .in1(bit_extender_1_out), .out(multiplexer_7_out), .sel(WriteFlag));
  Multiplexer #(.width(16)) multiplexer_8 (
    .in0(multiplexer_7_out), .in1(datamemory_1_dmdataout), .out(WriteBack), .sel(Mem2Reg));
  assign bit_extender_2_out = {{4{IMDataIn[11]}}, IMDataIn[11:0]};  // Bit_Extender bit_extender_2
  ALU alu_1 (.A(AluA), .B(AluB), .CarryIn(Cin), .ALUOp(ALUOp), .FlagsNZCV(ALUFlags), .Result(ALUResult));
  RegisterFile registerfile_1 (
    .CLK(CLKin), .A1(multiplexer_6_out), .WE3(RegW), .A3(multiplexer_3_out), .A2(IMDataIn[2:0]),
    .WD3(WriteBack), .Reset(Reset), .R7(instructionfetchunit_1_pcplus1), .RD1(AluA),
    .RD2(registerfile_1_rd2), .RD3(DMData));
  Multiplexer #(.width(16)) multiplexer_9 (
    .in0({16{1'b0}}), .in1(registerfile_1_rd2), .out(multiplexer_9_out), .sel(Offset));
  Multiplexer #(.width(16)) multiplexer_10 (
    .in0(multiplexer_9_out), .in1(bit_extender_2_out), .out(multiplexer_10_out), .sel(JMP));
  Multiplexer #(.width(16)) multiplexer_11 (
    .in0(multiplexer_10_out), .in1(bit_extender_2_out), .out(AluB), .sel(IMDataIn[15]));
  DataMemory datamemory_1 (
    .DMAddress(ALUResult), .WE(MemW), .CLK(CLKin), .DMDataIn(DMData), .DMDataOut(datamemory_1_dmdataout));

  assign DMAddress = ALUResult;
  assign IMData = IMDataIn;

  // Other names for the same wires on the sheet: A[15:0] = AluA; B[15:0] = AluB; move = IMDataIn[15];
  //   Result[15:0] = ALUResult

  // Notes on the sheet:
  //   Build your CPU here
endmodule

module FrontPanelController (
  input  Clk,
  input  Run,
  input  Step,
  input  Reset,
  input  Halt,
  output CpuClk,
  output RunHalt
);

  wire and_1_out, or_1_out, pull_resistor_1_node, t_ff_1_q;

  T_Flip_Flop t_ff_1 (.T(pull_resistor_1_node), .clk(Run), .Q(t_ff_1_q), .reset(Reset));  // open: Qn, preset
  Pull_Resistor #(.pull(1)) pull_resistor_1 (.node(pull_resistor_1_node));
  or or_1 (or_1_out, t_ff_1_q, Step);
  and and_1 (and_1_out, Clk, t_ff_1_q);
  and and_2 (RunHalt, or_1_out, ~Halt);  // AND_Gate
  Multiplexer multiplexer_1 (.in0(Step), .in1(and_1_out), .out(CpuClk), .sel(t_ff_1_q));
endmodule

module ALU (
  input  [15:0] A,
  input  [15:0] B,
  input  CarryIn,
  input  [3:0] ALUOp,
  output [3:0] FlagsNZCV,
  output [15:0] Result
);

  wire adder_1_cout, and_2_out, and_3_out, and_4_out, multiplexer_2_out, nand_1_out, or_2_out,
       subtractor_1_bout, xnor_1_out, xor_2_out;
  wire [15:0] adder_1_out, and_1_out, divider_1_out, divider_1_rem, multiplexer_1_out, multiplier_1_cout,
       multiplier_1_out, not_1_out, or_1_out, shifter_1_out, shifter_2_out, shifter_3_out, shifter_4_out,
       shifter_5_out, subtractor_1_out, xor_1_out;

  Adder #(.width(16)) adder_1 (.a(B), .b(A), .out(adder_1_out), .cout(adder_1_cout));  // open: cin
  Subtractor #(.width(16)) subtractor_1 (.a(A), .b(B), .out(subtractor_1_out), .bout(subtractor_1_bout));  // open: bin
  Multiplier #(.width(16)) multiplier_1 (.a(A), .b(B), .out(multiplier_1_out), .cout(multiplier_1_cout));  // open: cin
  Divider #(.width(16)) divider_1 (.a(A), .b(B), .out(divider_1_out), .rem(divider_1_rem));  // open: upper
  assign and_1_out = A & B;  // AND_Gate and_1, 16 bits wide
  assign or_1_out = A | B;  // OR_Gate or_1, 16 bits wide
  assign xor_1_out = A ^ B;  // XOR_Gate xor_1, 16 bits wide
  assign not_1_out = ~A;  // NOT_Gate not_1, 16 bits wide
  Shifter #(.width(16)) shifter_1 (.in(A), .\dist (B[3:0]), .out(shifter_1_out));
  Shifter #(.shift("lr"), .width(16)) shifter_2 (.in(A), .\dist (B[3:0]), .out(shifter_2_out));
  Shifter #(.shift("ar"), .width(16)) shifter_3 (.in(A), .\dist (B[3:0]), .out(shifter_3_out));
  Shifter #(.shift("rl"), .width(16)) shifter_4 (.in(A), .\dist (B[3:0]), .out(shifter_4_out));
  Shifter #(.shift("rr"), .width(16)) shifter_5 (.in(A), .\dist (B[3:0]), .out(shifter_5_out));
  Multiplexer #(.width(16)) multiplexer_1 (
    .in0(adder_1_out), .in1(subtractor_1_out), .out(multiplexer_1_out), .sel(ALUOp[0]));
  Multiplexer multiplexer_2 (.in0(adder_1_cout), .in1(subtractor_1_bout), .out(multiplexer_2_out), .sel(ALUOp[0]));
  NotExactlyOne xnor_1 (.out(xnor_1_out), .in0(B[15]), .in1(A[15]), .in2(ALUOp[0]));
  xor xor_2 (xor_2_out, B[15], multiplexer_1_out[15]);
  or or_2 (or_2_out, multiplier_1_cout[0], multiplier_1_cout[1], multiplier_1_cout[2], multiplier_1_cout[3], multiplier_1_cout[4], multiplier_1_cout[5], multiplier_1_cout[6], multiplier_1_cout[7], multiplier_1_cout[8], multiplier_1_cout[9], multiplier_1_cout[10], multiplier_1_cout[11], multiplier_1_cout[12], multiplier_1_cout[13], multiplier_1_cout[14], multiplier_1_cout[15]);
  Multiplexer #(.select(4), .width(16)) multiplexer_3 (
    .in0(adder_1_out), .in1(subtractor_1_out), .in2(multiplier_1_out), .in3(multiplier_1_cout),
    .in4(divider_1_out), .in5(divider_1_rem), .in6(and_1_out), .in7(or_1_out), .in8(xor_1_out),
    .in9(not_1_out), .in10(shifter_1_out), .in11(shifter_2_out), .in12(shifter_3_out), .in13(shifter_4_out),
    .in14(shifter_5_out), .in15(subtractor_1_out), .out({FlagsNZCV[3], Result[14:0]}), .sel(ALUOp));
  and and_2 (and_2_out, xnor_1_out, xor_2_out, nand_1_out);
  and and_3 (and_3_out, nand_1_out, multiplexer_2_out);
  nand nand_1 (nand_1_out, ALUOp[3], ALUOp[2], ALUOp[1]);
  and and_4 (and_4_out, ALUOp[3], ALUOp[2], ~ALUOp[1], ALUOp[0], or_2_out);  // AND_Gate
  or or_3 (FlagsNZCV[1], CarryIn, and_3_out);
  or or_4 (FlagsNZCV[0], and_4_out, and_2_out);
  nor nor_1 (FlagsNZCV[2], Result[0], Result[1], Result[2], Result[3], Result[4], Result[5], Result[6], Result[7], Result[8], Result[9], Result[10], Result[11], Result[12], Result[13], Result[14], FlagsNZCV[3]);

  assign Result[15] = FlagsNZCV[3];
endmodule

module InstructionFetchUnit (
  input  [15:0] WBBus,
  input  JMP,
  input  CLK,
  input  RESET,
  output [15:0] IMAddress,
  output [15:0] PCPlus1
);

  wire [15:0] multiplexer_1_out;

  Multiplexer #(.width(16)) multiplexer_1 (.in0(PCPlus1), .in1(WBBus), .out(multiplexer_1_out), .sel(JMP));
  Register #(.width(16)) R7 (.D(multiplexer_1_out), .clk(CLK), .Q(IMAddress), .clr(RESET));  // open: en
  Adder #(.width(16)) adder_1 (.a(IMAddress), .b(16'h1), .out(PCPlus1));  // open: cin, cout
endmodule

module RegisterFile (
  input  CLK,
  input  [2:0] A1,
  input  WE3,
  input  [2:0] A3,
  input  [2:0] A2,
  input  [15:0] WD3,
  input  Reset,
  input  [15:0] R7,
  output [15:0] RD1,
  output [15:0] RD2,
  output [15:0] RD3
);

  wire demultiplexer_1_out0, demultiplexer_1_out1, demultiplexer_1_out2, demultiplexer_1_out3,
       demultiplexer_1_out4, demultiplexer_1_out5, demultiplexer_1_out6;
  wire [15:0] R0_q, R1_q, R2_q, R3_q, R4_q, R5_q, R6_q;

  Demultiplexer #(.select(3)) demultiplexer_1 (
    .out0(demultiplexer_1_out0), .out1(demultiplexer_1_out1), .out2(demultiplexer_1_out2),
    .out3(demultiplexer_1_out3), .out4(demultiplexer_1_out4), .out5(demultiplexer_1_out5),
    .out6(demultiplexer_1_out6), .in(WE3), .sel(A3));  // open: out7
  Register #(.width(16)) R0 (.D(WD3), .en(demultiplexer_1_out0), .clk(CLK), .Q(R0_q), .clr(Reset));
  Register #(.width(16)) R1 (.D(WD3), .en(demultiplexer_1_out1), .clk(CLK), .Q(R1_q), .clr(Reset));
  Register #(.width(16)) R2 (.D(WD3), .en(demultiplexer_1_out2), .clk(CLK), .Q(R2_q), .clr(Reset));
  Register #(.width(16)) R3 (.D(WD3), .en(demultiplexer_1_out3), .clk(CLK), .Q(R3_q), .clr(Reset));
  Register #(.width(16)) R4 (.D(WD3), .en(demultiplexer_1_out4), .clk(CLK), .Q(R4_q), .clr(Reset));
  Register #(.width(16)) R5 (.D(WD3), .en(demultiplexer_1_out5), .clk(CLK), .Q(R5_q), .clr(Reset));
  Register #(.width(16)) R6 (.D(WD3), .en(demultiplexer_1_out6), .clk(CLK), .Q(R6_q), .clr(Reset));
  Multiplexer #(.select(3), .width(16)) multiplexer_1 (
    .in0(R0_q), .in1(R1_q), .in2(R2_q), .in3(R3_q), .in4(R4_q), .in5(R5_q), .in6(R6_q), .in7(R7), .out(RD1),
    .sel(A1));
  Multiplexer #(.select(3), .width(16)) multiplexer_2 (
    .in0(R0_q), .in1(R1_q), .in2(R2_q), .in3(R3_q), .in4(R4_q), .in5(R5_q), .in6(R6_q), .in7(R7), .out(RD2),
    .sel(A2));
  Multiplexer #(.select(3), .width(16)) multiplexer_3 (
    .in0(R0_q), .in1(R1_q), .in2(R2_q), .in3(R3_q), .in4(R4_q), .in5(R5_q), .in6(R6_q), .in7(R7), .out(RD3),
    .sel(A3));
endmodule

module DataMemory (
  input  [15:0] DMAddress,
  input  WE,
  input  CLK,
  input  [15:0] DMDataIn,
  output [15:0] DMDataOut
);

  RAM #(.addrWidth(16), .asyncread("true"), .dataWidth(16)) ram_1 (
    .addr(DMAddress), .we(WE), .clk(CLK), .din(DMDataIn), .dout(DMDataOut));  // open: oe
endmodule

module DecoderController (
  input  [6:0] CBits,
  input  [3:0] Flags,
  input  CLK,
  input  R,
  output MoveFlag,
  output [3:0] ALUOp,
  output WriteResult,
  output RegW,
  output Cin,
  output [3:0] LatchFlags,
  output JMP,
  output STOP,
  output WBranchOrResult,
  output WriteFlag,
  output MemW,
  output Offset,
  output Mem2Reg
);

  wire and_2_out, and_3_out, and_4_out, and_5_out, and_6_out, and_7_out, and_8_out, and_9_out, and_11_out,
       and_14_out, and_15_out, and_16_out, and_17_out, and_19_out, or_1_out, or_3_out, or_4_out, or_5_out;

  or or_1 (or_1_out, MoveFlag, WriteResult);
  Register #(.width(4)) register_1 (
    .D(Flags), .en(or_1_out), .clk(CLK), .Q({LatchFlags[3:2], Cin, LatchFlags[0]}), .clr(R));
  nor nor_1 (Offset, and_4_out, and_5_out);
  and and_1 (MoveFlag, ~CBits[6], ~CBits[5], ~CBits[4], ~CBits[3], CBits[2], CBits[1], CBits[0]);  // AND_Gate
  and and_2 (and_2_out, ~CBits[6], ~CBits[5], CBits[4], CBits[3], CBits[2], CBits[1], CBits[0]);  // AND_Gate
  or or_2 (MemW, and_3_out, and_4_out);
  and and_3 (and_3_out, ~CBits[6], ~CBits[5], ~CBits[4], CBits[3], CBits[2], ~CBits[1], ~CBits[0]);  // AND_Gate
  and and_4 (and_4_out, ~CBits[6], ~CBits[5], ~CBits[4], CBits[3], CBits[2], CBits[1], CBits[0]);  // AND_Gate
  and and_5 (and_5_out, ~CBits[6], ~CBits[5], ~CBits[4], CBits[3], ~CBits[2], CBits[1], CBits[0]);  // AND_Gate
  and and_6 (and_6_out, CBits[4], ~CBits[5], ~CBits[6]);  // AND_Gate
  or or_3 (or_3_out, and_7_out, JMP);
  and and_7 (and_7_out, ~CBits[6], ~CBits[5], ~CBits[4], CBits[3]);  // AND_Gate
  and and_8 (and_8_out, ~CBits[3], LatchFlags[2]);  // AND_Gate
  and and_9 (and_9_out, ~LatchFlags[2], CBits[3]);  // AND_Gate
  Multiplexer #(.width(4)) multiplexer_1 (.in0(CBits[3:0]), .in1(4'b0000), .out(ALUOp), .sel(or_3_out));
  and and_10 (WriteResult, CBits[4], ~CBits[5], ~CBits[6]);  // AND_Gate
  or or_4 (or_4_out, and_6_out, CBits[6]);
  or or_5 (or_5_out, and_8_out, and_9_out, ~CBits[4]);  // OR_Gate
  and and_11 (and_11_out, or_5_out, CBits[5], ~CBits[6]);  // AND_Gate
  and and_12 (WBranchOrResult, CBits[6], CBits[5], CBits[4], CBits[3]);
  and and_13 (WriteFlag, ~CBits[6], ~CBits[5], ~CBits[4], ~CBits[3], CBits[2], CBits[1], ~CBits[0]);  // AND_Gate
  and and_14 (and_14_out, CBits[0], CBits[1], ~CBits[2], CBits[3], ~CBits[4], ~CBits[5], ~CBits[6]);  // AND_Gate
  and and_15 (and_15_out, or_4_out, ~and_2_out);  // AND_Gate
  and and_16 (and_16_out, ~CBits[6], ~CBits[5], ~CBits[4], ~CBits[3], CBits[2], ~CBits[1], ~CBits[0]);  // AND_Gate
  and and_17 (and_17_out, ~CBits[6], ~CBits[5], ~CBits[4], ~CBits[3], CBits[2], CBits[1], ~CBits[0]);  // AND_Gate
  or or_6 (JMP, and_11_out, WBranchOrResult);
  and and_18 (STOP, ~CBits[6], ~CBits[5], ~CBits[4], ~CBits[3], ~CBits[2], CBits[1], CBits[0]);  // AND_Gate
  and and_19 (and_19_out, ~CBits[0], ~CBits[1], ~CBits[2], CBits[3], ~CBits[4], ~CBits[5], ~CBits[6]);  // AND_Gate
  or or_7 (Mem2Reg, and_19_out, and_14_out);
  or or_8 (RegW, and_15_out, and_16_out, and_17_out, Mem2Reg);

  assign LatchFlags[1] = Cin;
endmodule

module DecimalIO (
  input  [15:0] DMData,
  input  [15:0] DMAddress,
  input  CLK,
  input  Reset,
  output [15:0] Data
);

  wire and_1_out;

  and and_1 (and_1_out, DMAddress[0], DMAddress[1], DMAddress[2], DMAddress[3], DMAddress[4], DMAddress[5], DMAddress[6], DMAddress[7], DMAddress[8], DMAddress[9], DMAddress[10], DMAddress[11], DMAddress[12], DMAddress[13], DMAddress[14], DMAddress[15]);
  Register #(.width(16)) register_1 (.D(DMData), .en(and_1_out), .clk(CLK), .Q(Data), .clr(Reset));
endmodule

module DecimalDisplayControl (
  input  [15:0] DataIn,
  output [3:0] D0,
  output [3:0] D1,
  output [3:0] D2,
  output [3:0] D3,
  output [3:0] D4,
  output Sign
);

  wire add3ornah_1_out_5, add3ornah_1_out_6, add3ornah_1_out_7, add3ornah_1_out_8, add3ornah_2_out_5,
       add3ornah_2_out_6, add3ornah_2_out_7, add3ornah_2_out_8, add3ornah_3_out_5, add3ornah_3_out_6,
       add3ornah_3_out_7, add3ornah_3_out_8, add3ornah_4_out_5, add3ornah_4_out_6, add3ornah_4_out_7,
       add3ornah_4_out_8, add3ornah_5_out_5, add3ornah_5_out_6, add3ornah_5_out_7, add3ornah_5_out_8,
       add3ornah_6_out_5, add3ornah_6_out_6, add3ornah_6_out_7, add3ornah_6_out_8, add3ornah_7_out_5,
       add3ornah_7_out_6, add3ornah_7_out_7, add3ornah_7_out_8, add3ornah_8_out_5, add3ornah_8_out_6,
       add3ornah_8_out_7, add3ornah_8_out_8, add3ornah_9_out_5, add3ornah_9_out_6, add3ornah_9_out_7,
       add3ornah_9_out_8, add3ornah_10_out_5, add3ornah_10_out_6, add3ornah_10_out_7, add3ornah_10_out_8,
       add3ornah_11_out_5, add3ornah_11_out_6, add3ornah_11_out_7, add3ornah_11_out_8, add3ornah_12_out_5,
       add3ornah_12_out_6, add3ornah_12_out_7, add3ornah_12_out_8, add3ornah_13_out_5, add3ornah_13_out_6,
       add3ornah_13_out_7, add3ornah_13_out_8, add3ornah_14_out_5, add3ornah_14_out_6, add3ornah_14_out_7,
       add3ornah_14_out_8, add3ornah_15_out_5, add3ornah_15_out_6, add3ornah_15_out_7, add3ornah_15_out_8,
       add3ornah_16_out_5, add3ornah_16_out_6, add3ornah_16_out_7, add3ornah_16_out_8, add3ornah_17_out_5,
       add3ornah_17_out_6, add3ornah_17_out_7, add3ornah_17_out_8, add3ornah_18_out_5, add3ornah_18_out_6,
       add3ornah_18_out_7, add3ornah_18_out_8, add3ornah_19_out_5, add3ornah_19_out_6, add3ornah_19_out_7,
       add3ornah_19_out_8, add3ornah_20_out_5, add3ornah_20_out_6, add3ornah_20_out_7, add3ornah_20_out_8,
       add3ornah_21_out_5, add3ornah_21_out_6, add3ornah_21_out_7, add3ornah_21_out_8, add3ornah_22_out_5,
       add3ornah_22_out_6, add3ornah_22_out_7, add3ornah_23_out_5, add3ornah_23_out_6, add3ornah_23_out_7,
       add3ornah_23_out_8, add3ornah_24_out_5, add3ornah_24_out_6, add3ornah_24_out_7, add3ornah_24_out_8,
       add3ornah_25_out_5, add3ornah_25_out_6, add3ornah_25_out_7, add3ornah_25_out_8, add3ornah_26_out_5,
       add3ornah_26_out_6, add3ornah_26_out_7, add3ornah_27_out_5, add3ornah_27_out_6, add3ornah_27_out_7,
       add3ornah_27_out_8, add3ornah_28_out_5, add3ornah_28_out_6, add3ornah_28_out_7, add3ornah_28_out_8,
       add3ornah_29_out_5, add3ornah_29_out_6, add3ornah_29_out_7, add3ornah_29_out_8, add3ornah_30_out_5,
       add3ornah_30_out_6, add3ornah_30_out_7;
  wire [15:0] adder_1_out, not_1_out;
  wire [15:1] multiplexer_1_out;

  assign not_1_out = ~DataIn;  // NOT_Gate not_1, 16 bits wide
  Multiplexer #(.width(16)) multiplexer_1 (
    .in0(DataIn), .in1(adder_1_out), .out({multiplexer_1_out, D0[0]}), .sel(DataIn[15]));
  Adder #(.width(16)) adder_1 (.a(not_1_out), .b(16'h1), .out(adder_1_out));  // open: cin, cout
  Add3OrNah add3ornah_1 (
    .in_1(multiplexer_1_out[13]), .in_2(multiplexer_1_out[14]), .in_3(multiplexer_1_out[15]), .in_4(1'b0),
    .out_5(add3ornah_1_out_5), .out_6(add3ornah_1_out_6), .out_7(add3ornah_1_out_7), .out_8(add3ornah_1_out_8));
  Add3OrNah add3ornah_2 (
    .in_1(multiplexer_1_out[12]), .in_2(add3ornah_1_out_5), .in_3(add3ornah_1_out_6),
    .in_4(add3ornah_1_out_7), .out_5(add3ornah_2_out_5), .out_6(add3ornah_2_out_6),
    .out_7(add3ornah_2_out_7), .out_8(add3ornah_2_out_8));
  Add3OrNah add3ornah_3 (
    .in_1(multiplexer_1_out[11]), .in_2(add3ornah_2_out_5), .in_3(add3ornah_2_out_6),
    .in_4(add3ornah_2_out_7), .out_5(add3ornah_3_out_5), .out_6(add3ornah_3_out_6),
    .out_7(add3ornah_3_out_7), .out_8(add3ornah_3_out_8));
  Add3OrNah add3ornah_4 (
    .in_1(multiplexer_1_out[10]), .in_2(add3ornah_3_out_5), .in_3(add3ornah_3_out_6),
    .in_4(add3ornah_3_out_7), .out_5(add3ornah_4_out_5), .out_6(add3ornah_4_out_6),
    .out_7(add3ornah_4_out_7), .out_8(add3ornah_4_out_8));
  Add3OrNah add3ornah_5 (
    .in_1(add3ornah_3_out_8), .in_2(add3ornah_2_out_8), .in_3(add3ornah_1_out_8), .in_4(1'b0),
    .out_5(add3ornah_5_out_5), .out_6(add3ornah_5_out_6), .out_7(add3ornah_5_out_7), .out_8(add3ornah_5_out_8));
  Add3OrNah add3ornah_6 (
    .in_1(multiplexer_1_out[9]), .in_2(add3ornah_4_out_5), .in_3(add3ornah_4_out_6),
    .in_4(add3ornah_4_out_7), .out_5(add3ornah_6_out_5), .out_6(add3ornah_6_out_6),
    .out_7(add3ornah_6_out_7), .out_8(add3ornah_6_out_8));
  Add3OrNah add3ornah_7 (
    .in_1(add3ornah_4_out_8), .in_2(add3ornah_5_out_5), .in_3(add3ornah_5_out_6), .in_4(add3ornah_5_out_7),
    .out_5(add3ornah_7_out_5), .out_6(add3ornah_7_out_6), .out_7(add3ornah_7_out_7), .out_8(add3ornah_7_out_8));
  Add3OrNah add3ornah_8 (
    .in_1(multiplexer_1_out[8]), .in_2(add3ornah_6_out_5), .in_3(add3ornah_6_out_6),
    .in_4(add3ornah_6_out_7), .out_5(add3ornah_8_out_5), .out_6(add3ornah_8_out_6),
    .out_7(add3ornah_8_out_7), .out_8(add3ornah_8_out_8));
  Add3OrNah add3ornah_9 (
    .in_1(add3ornah_6_out_8), .in_2(add3ornah_7_out_5), .in_3(add3ornah_7_out_6), .in_4(add3ornah_7_out_7),
    .out_5(add3ornah_9_out_5), .out_6(add3ornah_9_out_6), .out_7(add3ornah_9_out_7), .out_8(add3ornah_9_out_8));
  Add3OrNah add3ornah_10 (
    .in_1(multiplexer_1_out[7]), .in_2(add3ornah_8_out_5), .in_3(add3ornah_8_out_6),
    .in_4(add3ornah_8_out_7), .out_5(add3ornah_10_out_5), .out_6(add3ornah_10_out_6),
    .out_7(add3ornah_10_out_7), .out_8(add3ornah_10_out_8));
  Add3OrNah add3ornah_11 (
    .in_1(add3ornah_8_out_8), .in_2(add3ornah_9_out_5), .in_3(add3ornah_9_out_6), .in_4(add3ornah_9_out_7),
    .out_5(add3ornah_11_out_5), .out_6(add3ornah_11_out_6), .out_7(add3ornah_11_out_7),
    .out_8(add3ornah_11_out_8));
  Add3OrNah add3ornah_12 (
    .in_1(add3ornah_9_out_8), .in_2(add3ornah_7_out_8), .in_3(add3ornah_5_out_8), .in_4(1'b0),
    .out_5(add3ornah_12_out_5), .out_6(add3ornah_12_out_6), .out_7(add3ornah_12_out_7),
    .out_8(add3ornah_12_out_8));
  Add3OrNah add3ornah_13 (
    .in_1(multiplexer_1_out[6]), .in_2(add3ornah_10_out_5), .in_3(add3ornah_10_out_6),
    .in_4(add3ornah_10_out_7), .out_5(add3ornah_13_out_5), .out_6(add3ornah_13_out_6),
    .out_7(add3ornah_13_out_7), .out_8(add3ornah_13_out_8));
  Add3OrNah add3ornah_14 (
    .in_1(add3ornah_10_out_8), .in_2(add3ornah_11_out_5), .in_3(add3ornah_11_out_6),
    .in_4(add3ornah_11_out_7), .out_5(add3ornah_14_out_5), .out_6(add3ornah_14_out_6),
    .out_7(add3ornah_14_out_7), .out_8(add3ornah_14_out_8));
  Add3OrNah add3ornah_15 (
    .in_1(add3ornah_11_out_8), .in_2(add3ornah_12_out_5), .in_3(add3ornah_12_out_6),
    .in_4(add3ornah_12_out_7), .out_5(add3ornah_15_out_5), .out_6(add3ornah_15_out_6),
    .out_7(add3ornah_15_out_7), .out_8(add3ornah_15_out_8));
  Add3OrNah add3ornah_16 (
    .in_1(multiplexer_1_out[5]), .in_2(add3ornah_13_out_5), .in_3(add3ornah_13_out_6),
    .in_4(add3ornah_13_out_7), .out_5(add3ornah_16_out_5), .out_6(add3ornah_16_out_6),
    .out_7(add3ornah_16_out_7), .out_8(add3ornah_16_out_8));
  Add3OrNah add3ornah_17 (
    .in_1(add3ornah_13_out_8), .in_2(add3ornah_14_out_5), .in_3(add3ornah_14_out_6),
    .in_4(add3ornah_14_out_7), .out_5(add3ornah_17_out_5), .out_6(add3ornah_17_out_6),
    .out_7(add3ornah_17_out_7), .out_8(add3ornah_17_out_8));
  Add3OrNah add3ornah_18 (
    .in_1(add3ornah_14_out_8), .in_2(add3ornah_15_out_5), .in_3(add3ornah_15_out_6),
    .in_4(add3ornah_15_out_7), .out_5(add3ornah_18_out_5), .out_6(add3ornah_18_out_6),
    .out_7(add3ornah_18_out_7), .out_8(add3ornah_18_out_8));
  Add3OrNah add3ornah_19 (
    .in_1(multiplexer_1_out[4]), .in_2(add3ornah_16_out_5), .in_3(add3ornah_16_out_6),
    .in_4(add3ornah_16_out_7), .out_5(add3ornah_19_out_5), .out_6(add3ornah_19_out_6),
    .out_7(add3ornah_19_out_7), .out_8(add3ornah_19_out_8));
  Add3OrNah add3ornah_20 (
    .in_1(add3ornah_16_out_8), .in_2(add3ornah_17_out_5), .in_3(add3ornah_17_out_6),
    .in_4(add3ornah_17_out_7), .out_5(add3ornah_20_out_5), .out_6(add3ornah_20_out_6),
    .out_7(add3ornah_20_out_7), .out_8(add3ornah_20_out_8));
  Add3OrNah add3ornah_21 (
    .in_1(add3ornah_17_out_8), .in_2(add3ornah_18_out_5), .in_3(add3ornah_18_out_6),
    .in_4(add3ornah_18_out_7), .out_5(add3ornah_21_out_5), .out_6(add3ornah_21_out_6),
    .out_7(add3ornah_21_out_7), .out_8(add3ornah_21_out_8));
  Add3OrNah add3ornah_22 (
    .in_1(add3ornah_18_out_8), .in_2(add3ornah_15_out_8), .in_3(add3ornah_12_out_8), .in_4(1'b0),
    .out_5(add3ornah_22_out_5), .out_6(add3ornah_22_out_6), .out_7(add3ornah_22_out_7), .out_8(D4[3]));
  Add3OrNah add3ornah_23 (
    .in_1(multiplexer_1_out[3]), .in_2(add3ornah_19_out_5), .in_3(add3ornah_19_out_6),
    .in_4(add3ornah_19_out_7), .out_5(add3ornah_23_out_5), .out_6(add3ornah_23_out_6),
    .out_7(add3ornah_23_out_7), .out_8(add3ornah_23_out_8));
  Add3OrNah add3ornah_24 (
    .in_1(add3ornah_19_out_8), .in_2(add3ornah_20_out_5), .in_3(add3ornah_20_out_6),
    .in_4(add3ornah_20_out_7), .out_5(add3ornah_24_out_5), .out_6(add3ornah_24_out_6),
    .out_7(add3ornah_24_out_7), .out_8(add3ornah_24_out_8));
  Add3OrNah add3ornah_25 (
    .in_1(add3ornah_20_out_8), .in_2(add3ornah_21_out_5), .in_3(add3ornah_21_out_6),
    .in_4(add3ornah_21_out_7), .out_5(add3ornah_25_out_5), .out_6(add3ornah_25_out_6),
    .out_7(add3ornah_25_out_7), .out_8(add3ornah_25_out_8));
  Add3OrNah add3ornah_26 (
    .in_1(add3ornah_21_out_8), .in_2(add3ornah_22_out_5), .in_3(add3ornah_22_out_6),
    .in_4(add3ornah_22_out_7), .out_5(add3ornah_26_out_5), .out_6(add3ornah_26_out_6),
    .out_7(add3ornah_26_out_7), .out_8(D4[2]));
  Add3OrNah add3ornah_27 (
    .in_1(multiplexer_1_out[2]), .in_2(add3ornah_23_out_5), .in_3(add3ornah_23_out_6),
    .in_4(add3ornah_23_out_7), .out_5(add3ornah_27_out_5), .out_6(add3ornah_27_out_6),
    .out_7(add3ornah_27_out_7), .out_8(add3ornah_27_out_8));
  Add3OrNah add3ornah_28 (
    .in_1(add3ornah_23_out_8), .in_2(add3ornah_24_out_5), .in_3(add3ornah_24_out_6),
    .in_4(add3ornah_24_out_7), .out_5(add3ornah_28_out_5), .out_6(add3ornah_28_out_6),
    .out_7(add3ornah_28_out_7), .out_8(add3ornah_28_out_8));
  Add3OrNah add3ornah_29 (
    .in_1(add3ornah_24_out_8), .in_2(add3ornah_25_out_5), .in_3(add3ornah_25_out_6),
    .in_4(add3ornah_25_out_7), .out_5(add3ornah_29_out_5), .out_6(add3ornah_29_out_6),
    .out_7(add3ornah_29_out_7), .out_8(add3ornah_29_out_8));
  Add3OrNah add3ornah_30 (
    .in_1(add3ornah_25_out_8), .in_2(add3ornah_26_out_5), .in_3(add3ornah_26_out_6),
    .in_4(add3ornah_26_out_7), .out_5(add3ornah_30_out_5), .out_6(add3ornah_30_out_6),
    .out_7(add3ornah_30_out_7), .out_8(D4[1]));
  Add3OrNah add3ornah_31 (
    .in_1(multiplexer_1_out[1]), .in_2(add3ornah_27_out_5), .in_3(add3ornah_27_out_6),
    .in_4(add3ornah_27_out_7), .out_5(D0[1]), .out_6(D0[2]), .out_7(D0[3]), .out_8(D1[0]));
  Add3OrNah add3ornah_32 (
    .in_1(add3ornah_27_out_8), .in_2(add3ornah_28_out_5), .in_3(add3ornah_28_out_6),
    .in_4(add3ornah_28_out_7), .out_5(D1[1]), .out_6(D1[2]), .out_7(D1[3]), .out_8(D2[0]));
  Add3OrNah add3ornah_33 (
    .in_1(add3ornah_28_out_8), .in_2(add3ornah_29_out_5), .in_3(add3ornah_29_out_6),
    .in_4(add3ornah_29_out_7), .out_5(D2[1]), .out_6(D2[2]), .out_7(D2[3]), .out_8(D3[0]));
  Add3OrNah add3ornah_34 (
    .in_1(add3ornah_29_out_8), .in_2(add3ornah_30_out_5), .in_3(add3ornah_30_out_6),
    .in_4(add3ornah_30_out_7), .out_5(D3[1]), .out_6(D3[2]), .out_7(D3[3]), .out_8(D4[0]));

  assign Sign = DataIn[15];
endmodule

module Add3OrNah (
  input  in_1,
  input  in_2,
  input  in_3,
  input  in_4,
  output out_5,
  output out_6,
  output out_7,
  output out_8
);

  wire comparator_1_gt;
  wire [3:0] adder_1_out;

  Adder #(.width(4)) adder_1 (.a({in_4, in_3, in_2, in_1}), .b(4'b0011), .out(adder_1_out));  // open: cin, cout
  Comparator #(.mode("unsigned"), .width(4)) comparator_1 (
    .a({in_4, in_3, in_2, in_1}), .b(4'b0100), .gt(comparator_1_gt));  // open: eq, lt
  Multiplexer #(.width(4)) multiplexer_1 (
    .in0({in_4, in_3, in_2, in_1}), .in1(adder_1_out), .out({out_8, out_7, out_6, out_5}),
    .sel(comparator_1_gt));
endmodule
